// Logisim project 3.circ as structural Verilog: 1 circuit, main circuit main
module main (
  input  in_1,
  input  in_2,
  input  in_3,
  input  in_4,
  output out_5
);

  wire and_1_out, multiplexer_1_out, multiplexer_2_out, nand_1_out, nor_1_out, or_1_out;

  or or_1 (or_1_out, in_2, in_1);
  nor nor_1 (nor_1_out, in_2, in_1);
  and and_1 (and_1_out, in_2, in_1);
  nand nand_1 (nand_1_out, in_2, in_1);
  Multiplexer multiplexer_1 (.in0(or_1_out), .in1(nor_1_out), .out(multiplexer_1_out), .sel(in_3));  // open: en
  Multiplexer multiplexer_2 (.in0(and_1_out), .in1(nand_1_out), .out(multiplexer_2_out), .sel(in_3));  // open: en
  Multiplexer multiplexer_3 (.in0(multiplexer_1_out), .in1(multiplexer_2_out), .out(out_5), .sel(in_4));  // open: en
endmodule
