// Logisim project 6.circ as structural Verilog: 1 circuit, main circuit main
module main (
  input  [1:0] in_1,
  input  [1:0] in_2,
  output out_3,
  output out_4,
  output out_5
);

  wire [1:0] xnor_1_out, xor_1_out;

  assign xor_1_out = in_2 ^ in_1;  // XOR_Gate xor_1, 2 bits wide
  assign xnor_1_out = ~(in_2 ^ in_1);  // XNOR_Gate xnor_1, 2 bits wide
  Comparator #(.width(2)) comparator_1 (.a(xor_1_out), .b(xnor_1_out), .gt(out_3), .eq(out_4), .lt(out_5));
endmodule
