// Logisim project 7.circ as structural Verilog: 1 circuit, main circuit main
module main (
  input  [1:0] in_1,
  input  [1:0] in_2,
  input  in_3,
  input  in_4,
  output out_5,
  output out_6
);

  wire [1:0] and_1_out, multiplexer_1_out, multiplexer_2_out, not_1_out, not_2_out, or_1_out;

  assign not_1_out = ~in_2;  // NOT_Gate not_1, 2 bits wide
  assign not_2_out = ~in_1;  // NOT_Gate not_2, 2 bits wide
  assign and_1_out = in_2 & in_1;  // AND_Gate and_1, 2 bits wide
  assign or_1_out = in_2 | in_1;  // OR_Gate or_1, 2 bits wide
  Multiplexer #(.width(2)) multiplexer_1 (
    .in0(not_1_out), .in1(not_2_out), .out(multiplexer_1_out), .sel(in_3));  // open: en
  Multiplexer #(.width(2)) multiplexer_2 (
    .in0(and_1_out), .in1(or_1_out), .out(multiplexer_2_out), .sel(in_4));  // open: en
  Comparator #(.width(2)) comparator_1 (
    .a(multiplexer_1_out), .b(multiplexer_2_out), .gt(out_5), .lt(out_6));  // open: eq
endmodule
