// Logisim project 2.circ as structural Verilog: 1 circuit, main circuit main
module main (
  input  in_1,
  input  in_2,
  input  in_3,
  output out_4
);

  wire nor_1_out, or_1_out;

  or or_1 (or_1_out, in_2, in_1);
  nor nor_1 (nor_1_out, in_2, in_1);
  Multiplexer multiplexer_1 (.in0(or_1_out), .in1(nor_1_out), .out(out_4), .sel(in_3));  // open: en
endmodule
