// Logisim project 4.circ as structural Verilog: 1 circuit, main circuit main
module main (
  input  in_1,
  input  in_2,
  input  [1:0] in_3,
  output out_4
);

  wire nor_1_out, or_1_out, xnor_1_out, xor_1_out;

  or or_1 (or_1_out, in_2, in_1);
  nor nor_1 (nor_1_out, in_2, in_1);
  xor xor_1 (xor_1_out, in_2, in_1);
  xnor xnor_1 (xnor_1_out, in_2, in_1);
  Multiplexer #(.select(2)) multiplexer_1 (
    .in0(or_1_out), .in1(nor_1_out), .in2(xor_1_out), .in3(xnor_1_out), .out(out_4), .sel(in_3));  // open: en
endmodule
