// Logisim project Q2.circ as structural Verilog: 1 circuit, main circuit main
module main (
  input  in_1,
  input  in_2,
  input  in_3,
  input  in_4,
  input  in_5,
  input  in_6,
  input  in_7,
  input  in_8,
  output out_9,
  output out_10,
  output out_11,
  output out_12,
  output out_13
);

  wire subtractor_1_bout, subtractor_2_bout, subtractor_3_bout;

  Subtractor #(.width(1)) subtractor_1 (.a(in_1), .b(in_5), .out(out_9), .bout(subtractor_1_bout));  // open: bin
  Subtractor #(.width(1)) subtractor_2 (
    .a(in_2), .b(in_6), .out(out_10), .bin(subtractor_1_bout), .bout(subtractor_2_bout));
  Subtractor #(.width(1)) subtractor_3 (
    .a(in_3), .b(in_7), .out(out_11), .bin(subtractor_2_bout), .bout(subtractor_3_bout));
  Subtractor #(.width(1)) subtractor_4 (.a(in_4), .b(in_8), .out(out_12), .bin(subtractor_3_bout), .bout(out_13));
endmodule
