// Logisim project Q4.circ as structural Verilog: 1 circuit, main circuit main
module main (
  input  in_1,
  input  in_2,
  input  in_3,
  input  in_4,
  input  in_5,
  input  in_6,
  input  in_7,
  input  in_8,
  output out_9,
  output out_10,
  output out_11,
  output out_12
);

  wire comparator_1_gt, comparator_1_lt, comparator_2_gt, comparator_2_lt, comparator_3_gt, comparator_3_lt,
       comparator_4_gt, comparator_4_lt;

  Comparator #(.width(1)) comparator_1 (.a(in_1), .b(in_5), .gt(comparator_1_gt), .lt(comparator_1_lt));  // open: eq
  Comparator #(.width(1)) comparator_2 (.a(in_2), .b(in_6), .gt(comparator_2_gt), .lt(comparator_2_lt));  // open: eq
  Comparator #(.width(1)) comparator_3 (.a(in_3), .b(in_7), .gt(comparator_3_gt), .lt(comparator_3_lt));  // open: eq
  Comparator #(.width(1)) comparator_4 (.a(in_4), .b(in_8), .gt(comparator_4_gt), .lt(comparator_4_lt));  // open: eq
  or or_1 (out_9, comparator_1_gt, comparator_1_lt);
  or or_2 (out_10, comparator_2_gt, comparator_2_lt);
  or or_3 (out_11, comparator_3_gt, comparator_3_lt);
  or or_4 (out_12, comparator_4_gt, comparator_4_lt);
endmodule
