// Logisim project Q3.circ as structural Verilog: 1 circuit, main circuit main
module main (
  input  in_1,
  input  in_2,
  input  in_3,
  input  in_4,
  input  in_5,
  input  in_6,
  input  in_7,
  input  in_8,
  output out_9,
  output out_10,
  output out_11,
  output out_12
);

  Comparator #(.width(1)) comparator_1 (.a(in_1), .b(in_5), .eq(out_9));  // open: gt, lt
  Comparator #(.width(1)) comparator_2 (.a(in_2), .b(in_6), .eq(out_10));  // open: gt, lt
  Comparator #(.width(1)) comparator_3 (.a(in_3), .b(in_7), .eq(out_11));  // open: gt, lt
  Comparator #(.width(1)) comparator_4 (.a(in_4), .b(in_8), .eq(out_12));  // open: gt, lt
endmodule
