// Logisim project Questao1.circ as structural Verilog: 2 circuits, main circuit main
module main (
  input  adress,
  input  R_W,
  input  CLEAR,
  input  [3:0] entrada,
  output [3:0] saida
);

  wire CLOCK_out;

  Clock CLOCK (.out(CLOCK_out));
  _1x1JK u_1x1jk_1 (
    .R_W(R_W), .CLOCK(CLOCK_out), .CLEAR(CLEAR), .ADRESS(adress), .\SAÍDA (saida[3]), .ENTRADA(entrada[3]));
  _1x1JK u_1x1jk_2 (
    .R_W(R_W), .CLOCK(CLOCK_out), .CLEAR(CLEAR), .ADRESS(adress), .\SAÍDA (saida[2]), .ENTRADA(entrada[2]));
  _1x1JK u_1x1jk_3 (
    .R_W(R_W), .CLOCK(CLOCK_out), .CLEAR(CLEAR), .ADRESS(adress), .\SAÍDA (saida[1]), .ENTRADA(entrada[1]));
  _1x1JK u_1x1jk_4 (
    .R_W(R_W), .CLOCK(CLOCK_out), .CLEAR(CLEAR), .ADRESS(adress), .\SAÍDA (saida[0]), .ENTRADA(entrada[0]));
endmodule

// 1x1
module _1x1JK (
  input  ADRESS,
  input  R_W,
  input  CLOCK,
  input  CLEAR,
  input  ENTRADA,
  output \SAÍDA 
);

  wire and_1_out, j_k_ff_1_q, not_1_out;

  and and_1 (and_1_out, ADRESS, R_W, CLOCK);
  not not_1 (not_1_out, ENTRADA);
  J_K_Flip_Flop j_k_ff_1 (
    .J(ENTRADA), .clk(and_1_out), .K(not_1_out), .Q(j_k_ff_1_q), .reset(CLEAR));  // open: Qn, preset
  and and_2 (\SAÍDA , ADRESS, j_k_ff_1_q);
endmodule
