// Logisim project Questao2.circ as structural Verilog: 3 circuits, main circuit main
module main (
  input  adress,
  input  R_W,
  input  CLEAR,
  input  [3:0] entrada,
  output [3:0] saida
);

  wire CLOCK_out;

  Clock CLOCK (.out(CLOCK_out));
  _1x2 u_1x2_1 (
    .R_W(R_W), .CLOCK(CLOCK_out), .CLEAR(CLEAR), .Adress(adress), .\saída1 (saida[2]), .\saída2 (saida[3]),
    .entrada1(entrada[2]), .entrada2(entrada[3]));
  _1x2 u_1x2_2 (
    .R_W(R_W), .CLOCK(CLOCK_out), .CLEAR(CLEAR), .Adress(adress), .\saída1 (saida[0]), .\saída2 (saida[1]),
    .entrada1(entrada[0]), .entrada2(entrada[1]));
endmodule

module _1x1 (
  input  ADRESS,
  input  R_W,
  input  CLOCK,
  input  CLEAR,
  input  ENTRADA,
  output \SAÍDA 
);

  wire and_1_out, j_k_ff_1_q, not_1_out;

  and and_1 (and_1_out, ADRESS, R_W, CLOCK);
  not not_1 (not_1_out, ENTRADA);
  J_K_Flip_Flop j_k_ff_1 (
    .J(ENTRADA), .clk(and_1_out), .K(not_1_out), .Q(j_k_ff_1_q), .reset(CLEAR));  // open: Qn, preset
  and and_2 (\SAÍDA , ADRESS, j_k_ff_1_q);
endmodule

module _1x2 (
  input  R_W,
  input  Adress,
  input  CLOCK,
  input  CLEAR,
  input  entrada1,
  input  entrada2,
  output \saída1 ,
  output \saída2 
);

  _1x1 u_1x1_1 (.R_W(R_W), .CLOCK(CLOCK), .CLEAR(CLEAR), .ADRESS(Adress), .\SAÍDA (\saída2 ), .ENTRADA(entrada2));
  _1x1 u_1x1_2 (.R_W(R_W), .CLOCK(CLOCK), .CLEAR(CLEAR), .ADRESS(Adress), .\SAÍDA (\saída1 ), .ENTRADA(entrada1));
endmodule
