// Logisim project Questao4.circ as structural Verilog
module main (
  input  [1:0] adress,
  input  R_W,
  input  clock,
  input  clear,
  input  [7:0] entrada,
  output [7:0] saida
);

  wire demultiplexer_1_out0, demultiplexer_1_out1, demultiplexer_1_out2, demultiplexer_1_out3;
  wire [3:0] \n2x4_1_saída , \n2x4_2_saída , \n2x4_3_saída , \n2x4_4_saída , \n2x4_6_saída , \n2x4_7_saída ,
       \n2x4_8_saída ;
  wire [7:4] \n2x4_5_saída ;

  Demultiplexer #(.select(2), .enable("false")) demultiplexer_1 (
    .out0(demultiplexer_1_out0), .out1(demultiplexer_1_out1), .out2(demultiplexer_1_out2),
    .out3(demultiplexer_1_out3), .in(1'b1), .sel(adress));
  _2x4 u_2x4_1 (
    .R_W(R_W), .CLOCK(clock), .CLEAR(clear), .adress(demultiplexer_1_out0), .entrada(entrada[7:4]),
    .\saída (\n2x4_1_saída ));
  _2x4 u_2x4_2 (
    .R_W(R_W), .CLOCK(clock), .CLEAR(clear), .adress(demultiplexer_1_out0), .entrada(entrada[3:0]),
    .\saída (\n2x4_2_saída ));
  _2x4 u_2x4_3 (
    .R_W(R_W), .CLOCK(clock), .CLEAR(clear), .adress(demultiplexer_1_out1), .entrada(entrada[7:4]),
    .\saída (\n2x4_3_saída ));
  _2x4 u_2x4_4 (
    .R_W(R_W), .CLOCK(clock), .CLEAR(clear), .adress(demultiplexer_1_out1), .entrada(entrada[3:0]),
    .\saída (\n2x4_4_saída ));
  _2x4 u_2x4_5 (
    .R_W(R_W), .CLOCK(clock), .CLEAR(clear), .adress(demultiplexer_1_out2), .entrada(entrada[7:4]),
    .\saída (\n2x4_5_saída ));
  _2x4 u_2x4_6 (
    .R_W(R_W), .CLOCK(clock), .CLEAR(clear), .adress(demultiplexer_1_out2), .entrada(entrada[3:0]),
    .\saída (\n2x4_6_saída ));
  _2x4 u_2x4_7 (
    .R_W(R_W), .CLOCK(clock), .CLEAR(clear), .adress(demultiplexer_1_out3), .entrada(entrada[7:4]),
    .\saída (\n2x4_7_saída ));
  _2x4 u_2x4_8 (
    .R_W(R_W), .CLOCK(clock), .CLEAR(clear), .adress(demultiplexer_1_out3), .entrada(entrada[3:0]),
    .\saída (\n2x4_8_saída ));
  Multiplexer #(.select(2), .width(8), .enable("false")) multiplexer_1 (
    .in0({\n2x4_1_saída , \n2x4_2_saída }), .in1({\n2x4_3_saída , \n2x4_4_saída }),
    .in2({\n2x4_5_saída , \n2x4_6_saída }), .in3({\n2x4_7_saída , \n2x4_8_saída }), .out(saida), .sel(adress));
endmodule

module _2x4 (
  input  adress,
  input  R_W,
  input  CLOCK,
  input  CLEAR,
  input  [3:0] entrada,
  output [3:0] \saída 
);

  wire demultiplexer_1_out0, demultiplexer_1_out1;
  wire [3:0] n1x4_1_saida, n1x4_2_saida;

  Demultiplexer #(.enable("false")) demultiplexer_1 (
    .out0(demultiplexer_1_out0), .out1(demultiplexer_1_out1), .in(1'b1), .sel(adress));
  _1x4 u_1x4_1 (
    .R_W(R_W), .CLOCK(CLOCK), .CLEAR(CLEAR), .adress(demultiplexer_1_out0), .saida(n1x4_1_saida),
    .entrada(entrada));
  _1x4 u_1x4_2 (
    .R_W(R_W), .CLOCK(CLOCK), .CLEAR(CLEAR), .adress(demultiplexer_1_out1), .saida(n1x4_2_saida),
    .entrada(entrada));
  Multiplexer #(.width(4), .enable("false")) multiplexer_1 (
    .in0(n1x4_1_saida), .in1(n1x4_2_saida), .out(\saída ), .sel(adress));
endmodule

module _1x2 (
  input  R_W,
  input  Adress,
  input  CLOCK,
  input  CLEAR,
  input  entrada1,
  input  entrada2,
  output \saída1 ,
  output \saída2 
);

  _1x1 u_1x1_1 (.R_W(R_W), .CLOCK(CLOCK), .CLEAR(CLEAR), .ADRESS(Adress), .\SAÍDA (\saída2 ), .ENTRADA(entrada2));
  _1x1 u_1x1_2 (.R_W(R_W), .CLOCK(CLOCK), .CLEAR(CLEAR), .ADRESS(Adress), .\SAÍDA (\saída1 ), .ENTRADA(entrada1));
endmodule

module _1x4 (
  input  adress,
  input  R_W,
  input  CLOCK,
  input  CLEAR,
  input  [3:0] entrada,
  output [3:0] saida
);

  _1x2 _1x2 (
    .R_W(R_W), .CLOCK(CLOCK), .CLEAR(CLEAR), .Adress(adress), .\saída1 (saida[2]), .\saída2 (saida[3]),
    .entrada1(entrada[2]), .entrada2(entrada[3]));
  _1x2 _1x2_2 (
    .R_W(R_W), .CLOCK(CLOCK), .CLEAR(CLEAR), .Adress(adress), .\saída1 (saida[0]), .\saída2 (saida[1]),
    .entrada1(entrada[0]), .entrada2(entrada[1]));
endmodule

module _1x1 (
  input  ADRESS,
  input  R_W,
  input  CLOCK,
  input  CLEAR,
  input  ENTRADA,
  output \SAÍDA 
);

  wire and_1_out, j_k_ff_1_q, not_1_out;

  and and_1 (and_1_out, ADRESS, R_W, CLOCK);
  not not_1 (not_1_out, ENTRADA);
  J_K_Flip_Flop j_k_ff_1 (
    .J(ENTRADA), .clk(and_1_out), .K(not_1_out), .Q(j_k_ff_1_q), .reset(CLEAR));  // open: Qn, preset
  and and_2 (\SAÍDA , ADRESS, j_k_ff_1_q);
endmodule
