// Logisim project Questao5.circ as structural Verilog: 1 circuit, main circuit main
module main (
  input  [2:0] adress,
  input  R_W,
  input  clock,
  input  clear,
  input  [7:0] entrada,
  output [7:0] out_6
);

  wire [1:0] demultiplexer_1_out0, demultiplexer_1_out1;
  wire [7:0] n4x8_1_p5, n4x8_2_p6;

  Demultiplexer #(.width(2), .enable("false")) demultiplexer_1 (
    .out0(demultiplexer_1_out0), .out1(demultiplexer_1_out1), .in(adress[1:0]), .sel(adress[2]));
  // _4x8 4x8_1: pin names not known; wires that end beside it: R_W, clock, clear, demultiplexer_1_out0, n4x8_1_p5, entrada
  // _4x8 4x8_2: pin names not known; wires that end beside it: R_W, clock, clear, entrada, demultiplexer_1_out1, n4x8_2_p6
  Multiplexer #(.width(8), .enable("false")) multiplexer_1 (
    .in0(n4x8_2_p6), .in1(n4x8_1_p5), .out(out_6), .sel(adress[2]));
endmodule
