// Logisim project Questao6.circ as structural Verilog: 5 circuits, main circuit main
module main (
  input  ADRESS,
  input  R_W,
  input  CLCK,
  input  CLEAR,
  input  [15:0] entrada,
  output [15:0] \saída 
);

  _1x8 u_1x8_1 (
    .R_W(R_W), .CLOCK(CLCK), .CLEAR(CLEAR), .adress(ADRESS), .entrada(entrada[7:0]), .\saída (\saída [15:8]));
  _1x8 u_1x8_2 (
    .R_W(R_W), .CLOCK(CLCK), .CLEAR(CLEAR), .adress(ADRESS), .entrada(entrada[15:8]), .\saída (\saída [7:0]));
endmodule

module _1x1 (
  input  ADRESS,
  input  R_W,
  input  CLOCK,
  input  CLEAR,
  input  ENTRADA,
  output \SAÍDA 
);

  wire and_1_out, j_k_ff_1_q, not_1_out;

  and and_1 (and_1_out, ADRESS, R_W, CLOCK);
  not not_1 (not_1_out, ENTRADA);
  J_K_Flip_Flop j_k_ff_1 (
    .J(ENTRADA), .clk(and_1_out), .K(not_1_out), .Q(j_k_ff_1_q), .reset(CLEAR));  // open: Qn, preset
  and and_2 (\SAÍDA , ADRESS, j_k_ff_1_q);
endmodule

module _1x2 (
  input  R_W,
  input  Adress,
  input  CLOCK,
  input  CLEAR,
  input  entrada1,
  input  entrada2,
  output \saída1 ,
  output \saída2 
);

  // _1x8_1x1 1x1_1: pin names not known; wires that end beside it: R_W, CLOCK, CLEAR, Adress, \saída2 , entrada2
  // _1x8_1x1 1x1_2: pin names not known; wires that end beside it: R_W, CLOCK, CLEAR, Adress, \saída1 , entrada1
endmodule

module _1x4 (
  input  adress,
  input  R_W,
  input  CLOCK,
  input  CLEAR,
  input  e1,
  input  e2,
  input  e3,
  input  e4,
  output s1,
  output s2,
  output s3,
  output s4
);

  // _1x8_1x2 _1x2: pin names not known; wires that end beside it: R_W, CLOCK, CLEAR, adress, s3, s4, e3, e4
  // _1x8_1x2 _1x2_2: pin names not known; wires that end beside it: R_W, CLOCK, CLEAR, adress, s1, s2, e1, e2
endmodule

module _1x8 (
  input  adress,
  input  R_W,
  input  CLOCK,
  input  CLEAR,
  input  [7:0] entrada,
  output [7:0] \saída 
);

  // _1x8_1x4 1x4_1: pin names not known; wires that end beside it: R_W, CLOCK, CLEAR, adress, \saída [4], \saída [5], \saída [6], \saída [7], entrada[4], entrada[5], entrada[6], entrada[7]
  // _1x8_1x4 1x4_2: pin names not known; wires that end beside it: R_W, CLOCK, CLEAR, adress, \saída [0], \saída [1], \saída [2], \saída [3], entrada[0], entrada[1], entrada[2], entrada[3]
endmodule
