// Logisim project questao1.circ as structural Verilog: 1 circuit, main circuit main
module main (
  input  _1,
  input  CLEAR
);

  wire CLOCK_out, j_k_ff_1_qn, j_k_ff_2_qn, j_k_ff_3_qn, j_k_ff_4_qn, j_k_ff_5_qn;

  Clock CLOCK (.out(CLOCK_out));
  // Probe on j_k_ff_1_qn
  // Probe on j_k_ff_2_qn
  J_K_Flip_Flop j_k_ff_1 (.J(_1), .clk(j_k_ff_2_qn), .K(_1), .Qn(j_k_ff_1_qn), .reset(CLEAR));  // open: Q, preset
  J_K_Flip_Flop j_k_ff_2 (.J(_1), .clk(j_k_ff_3_qn), .K(_1), .Qn(j_k_ff_2_qn), .reset(CLEAR));  // open: Q, preset
  // Probe on j_k_ff_3_qn
  J_K_Flip_Flop j_k_ff_3 (.J(_1), .clk(j_k_ff_4_qn), .K(_1), .Qn(j_k_ff_3_qn), .reset(CLEAR));  // open: Q, preset
  // Probe on j_k_ff_4_qn
  // Probe on j_k_ff_5_qn
  J_K_Flip_Flop j_k_ff_4 (.J(_1), .clk(j_k_ff_5_qn), .K(_1), .Qn(j_k_ff_4_qn), .reset(CLEAR));  // open: Q, preset
  J_K_Flip_Flop j_k_ff_5 (.J(_1), .clk(CLOCK_out), .K(_1), .Qn(j_k_ff_5_qn), .reset(CLEAR));  // open: Q, preset
endmodule
