// Logisim project questao2.circ as structural Verilog: 1 circuit, main circuit main
module main (
  input  _1,
  input  CLEAR
);

  wire CLOCK_out, j_k_ff_1_qn, j_k_ff_2_q, j_k_ff_2_qn, j_k_ff_3_q, j_k_ff_3_qn, j_k_ff_4_q, j_k_ff_4_qn,
       j_k_ff_5_q, j_k_ff_5_qn;

  Clock CLOCK (.out(CLOCK_out));
  // Probe on j_k_ff_1_qn
  J_K_Flip_Flop j_k_ff_1 (.J(_1), .clk(j_k_ff_2_q), .K(_1), .Qn(j_k_ff_1_qn), .reset(CLEAR));  // open: Q, preset
  J_K_Flip_Flop j_k_ff_2 (
    .J(_1), .clk(j_k_ff_3_q), .K(_1), .Q(j_k_ff_2_q), .Qn(j_k_ff_2_qn), .reset(CLEAR));  // open: preset
  // Probe on j_k_ff_2_qn
  J_K_Flip_Flop j_k_ff_3 (
    .J(_1), .clk(j_k_ff_4_q), .K(_1), .Q(j_k_ff_3_q), .Qn(j_k_ff_3_qn), .reset(CLEAR));  // open: preset
  // Probe on j_k_ff_3_qn
  // Probe on j_k_ff_4_qn
  J_K_Flip_Flop j_k_ff_4 (
    .J(_1), .clk(j_k_ff_5_q), .K(_1), .Q(j_k_ff_4_q), .Qn(j_k_ff_4_qn), .reset(CLEAR));  // open: preset
  J_K_Flip_Flop j_k_ff_5 (
    .J(_1), .clk(CLOCK_out), .K(_1), .Q(j_k_ff_5_q), .Qn(j_k_ff_5_qn), .reset(CLEAR));  // open: preset
  // Probe on j_k_ff_5_qn
endmodule
