// Logisim project questao4.circ as structural Verilog: 1 circuit, main circuit main
module main (
  input  _1
);

  wire and_1_out, j_k_ff_1_q, j_k_ff_1_qn, j_k_ff_2_q, j_k_ff_2_qn, j_k_ff_3_q, j_k_ff_3_qn, j_k_ff_4_q,
       j_k_ff_4_qn, not_1_out, not_2_out, not_3_out, or_1_out, PULSE_out;

  Clock PULSE (.out(PULSE_out));
  not not_1 (not_1_out, _1);
  or or_1 (or_1_out, not_1_out, and_1_out);
  and and_1 (and_1_out, not_2_out, j_k_ff_2_qn, not_3_out, j_k_ff_4_qn);
  not not_2 (not_2_out, j_k_ff_1_qn);
  not not_3 (not_3_out, j_k_ff_3_qn);
  // Probe on j_k_ff_4_q
  // Probe on j_k_ff_3_q
  J_K_Flip_Flop j_k_ff_1 (
    .J(_1), .clk(PULSE_out), .K(_1), .Q(j_k_ff_1_q), .Qn(j_k_ff_1_qn), .preset(or_1_out));  // open: reset
  // Probe on j_k_ff_2_q
  J_K_Flip_Flop j_k_ff_2 (
    .J(_1), .clk(j_k_ff_1_q), .K(_1), .Q(j_k_ff_2_q), .Qn(j_k_ff_2_qn), .preset(or_1_out));  // open: reset
  // Probe on j_k_ff_1_q
  J_K_Flip_Flop j_k_ff_3 (
    .J(_1), .clk(j_k_ff_2_q), .K(_1), .Q(j_k_ff_3_q), .Qn(j_k_ff_3_qn), .preset(or_1_out));  // open: reset
  J_K_Flip_Flop j_k_ff_4 (
    .J(_1), .clk(j_k_ff_3_q), .K(_1), .Q(j_k_ff_4_q), .Qn(j_k_ff_4_qn), .preset(or_1_out));  // open: reset
endmodule
