// Logisim project questao7.circ as structural Verilog: 1 circuit, main circuit main
module main (
  input  DATA,
  input  clear
);

  wire CLOCK_out, d_ff_1_q, d_ff_2_q, d_ff_3_q, d_ff_4_q, d_ff_5_q, d_ff_6_q, or_1_out;

  Clock CLOCK (.out(CLOCK_out));
  or or_1 (or_1_out, DATA, d_ff_6_q);
  D_Flip_Flop d_ff_1 (.clk(CLOCK_out), .D(or_1_out), .Q(d_ff_1_q), .reset(clear));  // open: Qn, preset
  // Probe on d_ff_1_q
  D_Flip_Flop d_ff_2 (.clk(CLOCK_out), .D(d_ff_1_q), .Q(d_ff_2_q), .reset(clear));  // open: Qn, preset
  // Probe on d_ff_2_q
  // Probe on d_ff_3_q
  D_Flip_Flop d_ff_3 (.clk(CLOCK_out), .D(d_ff_2_q), .Q(d_ff_3_q), .reset(clear));  // open: Qn, preset
  // Probe on d_ff_4_q
  D_Flip_Flop d_ff_4 (.clk(CLOCK_out), .D(d_ff_3_q), .Q(d_ff_4_q), .reset(clear));  // open: Qn, preset
  D_Flip_Flop d_ff_5 (.clk(CLOCK_out), .D(d_ff_4_q), .Q(d_ff_5_q), .reset(clear));  // open: Qn, preset
  // Probe on d_ff_5_q
  // Probe on d_ff_6_q
  D_Flip_Flop d_ff_6 (.clk(CLOCK_out), .D(d_ff_5_q), .Q(d_ff_6_q), .reset(clear));  // open: Qn, preset
endmodule
