// Logisim project questao2.circ as structural Verilog: 1 circuit, main circuit main
module main (
  input  DATA,
  input  CLEAR
);

  wire CLOCK_out, d_ff_1_q, d_ff_2_q, d_ff_3_q, d_ff_4_q, d_ff_5_q, d_ff_6_q;

  Clock CLOCK (.out(CLOCK_out));
  D_Flip_Flop d_ff_1 (.clk(CLOCK_out), .D(DATA), .Q(d_ff_1_q), .reset(CLEAR));  // open: Qn, preset
  // Probe on d_ff_1_q
  D_Flip_Flop d_ff_2 (.clk(CLOCK_out), .D(d_ff_1_q), .Q(d_ff_2_q), .reset(CLEAR));  // open: Qn, preset
  // Probe on d_ff_2_q
  D_Flip_Flop d_ff_3 (.clk(CLOCK_out), .D(d_ff_2_q), .Q(d_ff_3_q), .reset(CLEAR));  // open: Qn, preset
  // Probe on d_ff_3_q
  D_Flip_Flop d_ff_4 (.clk(CLOCK_out), .D(d_ff_3_q), .Q(d_ff_4_q), .reset(CLEAR));  // open: Qn, preset
  // Probe on d_ff_4_q
  D_Flip_Flop d_ff_5 (.clk(CLOCK_out), .D(d_ff_4_q), .Q(d_ff_5_q), .reset(CLEAR));  // open: Qn, preset
  // Probe on d_ff_5_q
  D_Flip_Flop d_ff_6 (.clk(CLOCK_out), .D(d_ff_5_q), .Q(d_ff_6_q), .reset(CLEAR));  // open: Qn, preset
  // Probe on d_ff_6_q
endmodule
