// Logisim project questao5.circ as structural Verilog: 1 circuit, main circuit main
module main (
  input  CLEAR,
  input  LOAD,
  input  DATA_0,
  input  DATA_1,
  input  DATA_5,
  input  DATA_2,
  input  DATA_3,
  input  DATA_4
);

  wire and_1_out, and_2_out, and_3_out, and_4_out, and_5_out, and_6_out, CLOCK_out, s_r_ff_1_q, s_r_ff_2_q,
       s_r_ff_3_q, s_r_ff_4_q, s_r_ff_5_q, s_r_ff_6_q;

  Clock CLOCK (.out(CLOCK_out));
  and and_1 (and_1_out, LOAD, DATA_0);
  // Probe on s_r_ff_1_q
  S_R_Flip_Flop s_r_ff_1 (.S(and_1_out), .clk(CLOCK_out), .R(1'b0), .Q(s_r_ff_1_q), .reset(CLEAR));  // open: Qn, preset
  // Probe on s_r_ff_2_q
  S_R_Flip_Flop s_r_ff_2 (
    .S(and_2_out), .clk(CLOCK_out), .R(s_r_ff_1_q), .Q(s_r_ff_2_q), .reset(CLEAR));  // open: Qn, preset
  and and_2 (and_2_out, LOAD, DATA_1);
  // Probe on s_r_ff_3_q
  S_R_Flip_Flop s_r_ff_3 (
    .S(and_3_out), .clk(CLOCK_out), .R(s_r_ff_2_q), .Q(s_r_ff_3_q), .reset(CLEAR));  // open: Qn, preset
  and and_3 (and_3_out, LOAD, DATA_2);
  and and_4 (and_4_out, LOAD, DATA_3);
  // Probe on s_r_ff_4_q
  S_R_Flip_Flop s_r_ff_4 (
    .S(and_4_out), .clk(CLOCK_out), .R(s_r_ff_3_q), .Q(s_r_ff_4_q), .reset(CLEAR));  // open: Qn, preset
  // Probe on s_r_ff_5_q
  S_R_Flip_Flop s_r_ff_5 (
    .S(and_5_out), .clk(CLOCK_out), .R(s_r_ff_4_q), .Q(s_r_ff_5_q), .reset(CLEAR));  // open: Qn, preset
  and and_5 (and_5_out, LOAD, DATA_4);
  and and_6 (and_6_out, LOAD, DATA_5);
  // Probe on s_r_ff_6_q
  S_R_Flip_Flop s_r_ff_6 (
    .S(and_6_out), .clk(CLOCK_out), .R(s_r_ff_5_q), .Q(s_r_ff_6_q), .reset(CLEAR));  // open: Qn, preset
endmodule
